# Fritzing sketch nano-node (saved by Fritzing 0.9.3b)
stripboards: 1

parts:
  Part4 = Bluetooth HM-10
  Part5 = Arduino Nano (Rev3.0)
  MPU9250_MPU-1 = SparkFun IMU Breakout - MPU-9250 [part_number=" SEN-13762"]
  U1 = Battery Holders [package=lipo-1100mAh]

nets:
  N1: Part4.RXD, Part5.D1/TX
  N2: Part4.TXD, Part5.D0/RX
  GND: Part4.GND, Part5.GND, MPU9250_MPU-1.GND, MPU9250_MPU-1.INT, U1.-
  VCC: Part4.VCC, Part5.3V3, MPU9250_MPU-1.VDD, MPU9250_MPU-1.!CS
  N3: Part4.STATE, Part5.D2
  N4: Part4.BRK, Part5.D3
  N5: Part5.VIN, U1.+
  N6: Part5.A5, MPU9250_MPU-1.SCL/SCLK, MPU9250_MPU-1.VDDIO
  N7: Part5.A4, MPU9250_MPU-1.SDA/SDI, MPU9250_MPU-1.AD0/SDO
